// Logisim project 16-bit ALU.circ as structural Verilog: 7 circuits, main circuit main
// ALU
module _16_bit_b (
  input  [15:0] A,
  input  [15:0] B,
  input  ALUop,
  input  [2:0] Operation,
  input  Cin,
  input  Cin_2,
  output [15:0] Result,
  output Result_2,
  output Cout,
  output Cout_2
);

  wire comparator_1_lt, subtractor_3_bout, undriven;
  wire [15:0] adder_1_out, AND_out, bit_extender_1_out, NOR_out, OR_out, subtractor_1_out, subtractor_3_out,
       XOR_out;

  assign AND_out = A & B;  // AND_Gate AND, 16 bits wide
  assign OR_out = A | B;  // OR_Gate OR, 16 bits wide
  assign XOR_out = A ^ B;  // XOR_Gate XOR, 16 bits wide
  assign NOR_out = ~(A | B);  // NOR_Gate NOR, 16 bits wide
  Adder #(.width(16)) adder_1 (.a(A), .b(B), .out(adder_1_out), .cin(Cin), .cout(Cout));
  Subtractor #(.width(16)) subtractor_1 (.a(A), .b(B), .out(subtractor_1_out), .bin(Cin_2), .bout(Cout_2));
  Subtractor #(.width(16)) subtractor_2 (.a(A), .b(B), .out(subtractor_1_out), .bin(Cin_2), .bout(Cout_2));
  Subtractor #(.width(16)) subtractor_3 (
    .a(A), .b(B), .out(subtractor_3_out), .bin(undriven), .bout(subtractor_3_bout));
  Subtractor #(.width(16)) subtractor_4 (
    .a(A), .b(B), .out(subtractor_3_out), .bin(undriven), .bout(subtractor_3_bout));
  Comparator #(.width(16)) comparator_1 (.a(A), .b(B), .lt(comparator_1_lt));  // open: gt, eq
  Multiplexer #(.select(3), .width(16)) multiplexer_1 (
    .in0(AND_out), .in1(OR_out), .in2(XOR_out), .in3(NOR_out), .in4(adder_1_out), .in5(subtractor_1_out),
    .in6(bit_extender_1_out), .in7(subtractor_3_out), .out(Result), .sel(Operation), .en(ALUop));
  Multiplexer #(.select(3), .width(16)) multiplexer_2 (
    .in0(AND_out), .in1(OR_out), .in2(XOR_out), .in3(NOR_out), .in4(adder_1_out), .in5(subtractor_1_out),
    .in6(bit_extender_1_out), .in7(subtractor_3_out), .out(Result), .sel(Operation), .en(ALUop));
  assign bit_extender_1_out = {{15{1'b0}}, comparator_1_lt};  // Bit_Extender bit_extender_1
  assign bit_extender_1_out = {{15{1'b0}}, comparator_1_lt};  // Bit_Extender bit_extender_2
  nor nor_2 (Result_2, Result[0], Result[1], Result[2], Result[3], Result[4], Result[5], Result[6], Result[7], Result[8], Result[9], Result[10], Result[11], Result[12], Result[13], Result[14], Result[15]);
endmodule

module main (
  input  Cout
);

  wire ALUop, ALUSrc, and_1_out, branch, button_1_out, clock_1_out, control_unit_1_regwrite, Enable, jump,
       MemRead, MemReg, MemWrite, n16_bit_b_1_result_2, RegDst;
  wire [2:0] main_1_o0;
  wire [3:0] multiplexer_1_out, opcode;
  wire [11:0] adder_1_out, adder_2_out, bit_extender_2_out, multiplexer_4_out, ram_1_data, register_1_q, toPC;
  wire [15:0] bit_extender_1_out, multiplexer_2_out, multiplexer_3_out, n16_bit_b_1_result, ram_2_data,
       register_file_1_read_data_1, register_file_1_read_data_2;

  Control_Unit control_unit_1 (
    .ALUsrc(ALUSrc), .ALUop(ALUop), .memRead(MemRead), .memWrite(MemWrite),
    .RegWrite(control_unit_1_regwrite), .memToReg(MemReg), .RegDst(RegDst), .Branch(branch), .Jump(jump),
    .in_1(opcode));
  Register #(.width(12)) register_1 (.D(toPC), .Q(register_1_q), .clk(clock_1_out), .clr(button_1_out));  // open: en
  Button button_1 (.out(button_1_out));
  Clock clock_1 (.out(clock_1_out));
  Adder #(.width(12)) adder_1 (.a(register_1_q), .b(12'h1), .out(adder_1_out));  // open: cin, cout
  alu_control_main main_1 (
    .ALUop(ALUop), .O2(main_1_o0[2]), .I3(opcode[3]), .I2(opcode[2]), .O1(main_1_o0[1]), .I1(opcode[1]),
    .O0(main_1_o0[0]), .I0(opcode[0]), .Enable(Enable));
  RAM #(.addrWidth(12), .dataWidth(16)) ram_1 (
    .addr(register_1_q), .data({opcode, ram_1_data}));  // open: sel, clk, ld, clr
  Multiplexer #(.width(4), .enable("false")) multiplexer_1 (
    .in0(ram_1_data[7:4]), .in1(ram_1_data[3:0]), .out(multiplexer_1_out), .sel(RegDst));
  register_file register_file_1 (
    .Clock(clock_1_out), .read_data_1(register_file_1_read_data_1),
    .read_data_2(register_file_1_read_data_2), .RA(ram_1_data[11:8]), .write_register(multiplexer_1_out),
    .RB(ram_1_data[7:4]), .regWrite(control_unit_1_regwrite), .data(multiplexer_3_out));
  assign bit_extender_1_out = {{12{1'b0}}, ram_1_data[3:0]};  // Bit_Extender bit_extender_1
  // Probe on register_file_1_read_data_1
  // Probe on multiplexer_2_out
  Multiplexer #(.width(16), .enable("false")) multiplexer_2 (
    .in0(register_file_1_read_data_2), .in1(bit_extender_1_out), .out(multiplexer_2_out), .sel(ALUSrc));
  Bit_Extender #(.in_width(16), .out_width(12), .\type ("sign")) bit_extender_2 (
    .in(bit_extender_1_out), .out(bit_extender_2_out));
  Multiplexer #(.width(16), .enable("false")) multiplexer_3 (
    .in0(n16_bit_b_1_result), .in1(ram_2_data), .out(multiplexer_3_out), .sel(MemReg));
  _16_bit_b u_16_bit_b_1 (
    .B(multiplexer_2_out), .Result(n16_bit_b_1_result), .Result_2(n16_bit_b_1_result_2), .Cout_2(Cout),
    .Operation(main_1_o0), .A(register_file_1_read_data_1), .ALUop(Enable));  // open: Cin_2, Cout, Cin
  Adder #(.width(12)) adder_2 (.a(adder_1_out), .b(bit_extender_2_out), .out(adder_2_out));  // open: cin, cout
  and and_1 (and_1_out, branch, n16_bit_b_1_result_2);
  Multiplexer #(.width(12), .enable("false")) multiplexer_4 (
    .in0(adder_1_out), .in1(adder_2_out), .out(multiplexer_4_out), .sel(and_1_out));
  RAM #(.addrWidth(16), .dataWidth(16), .bus("separate")) ram_2 (
    .addr(n16_bit_b_1_result), .din(register_file_1_read_data_2), .data(ram_2_data), .str(MemWrite),
    .clk(clock_1_out), .ld(MemRead));  // open: sel, clr
  Multiplexer #(.width(12), .enable("false")) multiplexer_5 (
    .in0(multiplexer_4_out), .in1(ram_1_data), .out(toPC), .sel(jump));
endmodule

// 1- bit
module _1_bit_ALU (
  input  A,
  input  B,
  input  [2:0] Operation,
  input  Cin,
  input  Sub,
  input  Less,
  output Result,
  output Cout,
  output Set
);

  wire AND_out, NOR_out, OR_out, xor_1_out, XOR_2_out;

  xor xor_1 (xor_1_out, B, Sub);
  and AND (AND_out, A, B);
  or OR (OR_out, A, B);
  xor XOR_2 (XOR_2_out, A, B);
  nor NOR (NOR_out, A, B);
  Adder #(.width(1)) adder_1 (.a(A), .b(xor_1_out), .out(Set), .cin(Cin), .cout(Cout));
  Multiplexer #(.select(3)) multiplexer_1 (
    .in0(AND_out), .in1(OR_out), .in2(XOR_2_out), .in3(NOR_out), .in4(Set), .in5(Less), .out(Result),
    .sel(Operation));  // open: in6, in7, en
endmodule

// Register
module register_file (
  input  [3:0] write_register,
  input  [3:0] RA,
  input  [3:0] RB,
  input  [15:0] data,
  input  regWrite,
  input  Clock,
  output [15:0] read_data_1,
  output [15:0] read_data_2
);

  wire and_1_out, and_2_out, and_3_out, and_4_out, and_5_out, and_6_out, and_7_out, and_8_out, and_9_out,
       and_10_out, and_11_out, and_12_out, and_13_out, and_14_out, and_15_out, and_16_out, decoder_1_out0,
       decoder_1_out1, decoder_1_out2, decoder_1_out3, decoder_1_out4, decoder_1_out5, decoder_1_out6,
       decoder_1_out7, decoder_1_out8, decoder_1_out9, decoder_1_out10, decoder_1_out11, decoder_1_out12,
       decoder_1_out13, decoder_1_out14, decoder_1_out15;
  wire [15:0] a0_q, fp_q, gp_q, ra_q, s0_q, s1_q, s2_q, s3_q, s4_q, s5_q, sp_q, t0_q, t1_q, t2_q, t3_q,
       zero_q;

  Decoder #(.select(4)) decoder_1 (
    .out0(decoder_1_out0), .out1(decoder_1_out1), .out2(decoder_1_out2), .out3(decoder_1_out3),
    .out4(decoder_1_out4), .out5(decoder_1_out5), .out6(decoder_1_out6), .out7(decoder_1_out7),
    .out8(decoder_1_out8), .out9(decoder_1_out9), .out10(decoder_1_out10), .out11(decoder_1_out11),
    .out12(decoder_1_out12), .out13(decoder_1_out13), .out14(decoder_1_out14), .out15(decoder_1_out15),
    .sel(write_register));  // open: en
  and and_1 (and_1_out, decoder_1_out0, regWrite);
  and and_2 (and_2_out, decoder_1_out1, regWrite);
  and and_3 (and_3_out, decoder_1_out2, regWrite);
  and and_4 (and_4_out, decoder_1_out3, regWrite);
  and and_5 (and_5_out, decoder_1_out4, regWrite);
  and and_6 (and_6_out, decoder_1_out5, regWrite);
  and and_7 (and_7_out, decoder_1_out6, regWrite);
  and and_8 (and_8_out, decoder_1_out7, regWrite);
  Register #(.width(16)) zero (.D(data), .en(and_1_out), .Q(zero_q), .clk(Clock));  // open: clr
  Register #(.width(16)) t0 (.D(data), .en(and_2_out), .Q(t0_q), .clk(Clock));  // open: clr
  Register #(.width(16)) t1 (.D(data), .en(and_3_out), .Q(t1_q), .clk(Clock));  // open: clr
  Register #(.width(16)) t2 (.D(data), .en(and_4_out), .Q(t2_q), .clk(Clock));  // open: clr
  Register #(.width(16)) t3 (.D(data), .en(and_5_out), .Q(t3_q), .clk(Clock));  // open: clr
  Register #(.width(16)) s0 (.D(data), .en(and_6_out), .Q(s0_q), .clk(Clock));  // open: clr
  Register #(.width(16)) s1 (.D(data), .en(and_7_out), .Q(s1_q), .clk(Clock));  // open: clr
  Register #(.width(16)) s2 (.D(data), .en(and_8_out), .Q(s2_q), .clk(Clock));  // open: clr
  and and_9 (and_9_out, decoder_1_out8, regWrite);
  and and_10 (and_10_out, decoder_1_out9, regWrite);
  and and_11 (and_11_out, decoder_1_out10, regWrite);
  and and_12 (and_12_out, decoder_1_out11, regWrite);
  and and_13 (and_13_out, decoder_1_out12, regWrite);
  and and_14 (and_14_out, decoder_1_out13, regWrite);
  and and_15 (and_15_out, decoder_1_out14, regWrite);
  and and_16 (and_16_out, decoder_1_out15, regWrite);
  Register #(.width(16)) s3 (.D(data), .en(and_9_out), .Q(s3_q), .clk(Clock));  // open: clr
  Register #(.width(16)) s4 (.D(data), .en(and_10_out), .Q(s4_q), .clk(Clock));  // open: clr
  Register #(.width(16)) s5 (.D(data), .en(and_11_out), .Q(s5_q), .clk(Clock));  // open: clr
  Register #(.width(16)) gp (.D(data), .en(and_12_out), .Q(gp_q), .clk(Clock));  // open: clr
  Register #(.width(16)) sp (.D(data), .en(and_13_out), .Q(sp_q), .clk(Clock));  // open: clr
  Register #(.width(16)) fp (.D(data), .en(and_14_out), .Q(fp_q), .clk(Clock));  // open: clr
  Register #(.width(16)) u_ra (.D(data), .en(and_15_out), .Q(ra_q), .clk(Clock));  // open: clr
  Register #(.width(16)) a0 (.D(data), .en(and_16_out), .Q(a0_q), .clk(Clock));  // open: clr
  Multiplexer #(.select(4), .width(16)) multiplexer_1 (
    .in0(zero_q), .in1(t0_q), .in2(t1_q), .in3(t2_q), .in4(t3_q), .in5(s0_q), .in6(s1_q), .in7(s2_q),
    .in8(s3_q), .in9(s4_q), .in10(s5_q), .in11(gp_q), .in12(sp_q), .in13(fp_q), .in14(ra_q), .in15(a0_q),
    .out(read_data_1), .sel(RA));  // open: en
  Multiplexer #(.select(4), .width(16)) multiplexer_2 (
    .in0(zero_q), .in1(t0_q), .in2(t1_q), .in3(t2_q), .in4(t3_q), .in5(s0_q), .in6(s1_q), .in7(s2_q),
    .in8(s3_q), .in9(s4_q), .in10(s5_q), .in11(gp_q), .in12(sp_q), .in13(fp_q), .in14(ra_q), .in15(a0_q),
    .out(read_data_2), .sel(RB));  // open: en
endmodule

module Extend_block (
  input  [3:0] in_1,
  output ALUsrc,
  output ALUop,
  output memRead,
  output memWrite,
  output RegWrite,
  output memToReg,
  output RegDst,
  output Branch,
  output Jump
);

  wire and_1_out, and_2_out, and_3_out, and_4_out, and_5_out, nand_1_out, nand_2_out, nand_3_out, nand_4_out,
       nand_5_out, nand_6_out, nand_7_out, nand_8_out, nand_9_out, nand_10_out, nand_11_out, nand_12_out,
       nand_13_out, nand_14_out, nand_15_out, nand_16_out, nand_17_out, nand_18_out, nand_19_out,
       nand_20_out, nand_21_out, nand_22_out, nand_23_out, nand_24_out, nand_25_out, nand_26_out,
       nand_27_out, nand_28_out, nand_29_out, nand_30_out, nand_31_out, nand_32_out, not_1_out, not_2_out,
       not_3_out, not_4_out, not_5_out, not_6_out, not_7_out, not_8_out, not_9_out;

  not not_1 (not_1_out, in_1[1]);
  not not_2 (not_2_out, in_1[2]);
  not not_3 (not_3_out, in_1[1]);
  nand nand_1 (nand_1_out, in_1[2], in_1[2]);
  nand nand_2 (nand_2_out, in_1[1], in_1[1]);
  nand nand_3 (nand_3_out, in_1[0], in_1[0]);
  not not_4 (not_4_out, in_1[3]);
  not not_5 (not_5_out, in_1[2]);
  not not_6 (not_6_out, in_1[2]);
  not not_7 (not_7_out, in_1[1]);
  nand nand_4 (nand_4_out, in_1[3], in_1[3]);
  nand nand_5 (nand_5_out, in_1[2], in_1[2]);
  nand nand_6 (nand_6_out, in_1[3], in_1[3]);
  nand nand_7 (nand_7_out, in_1[0], in_1[0]);
  nand nand_8 (nand_8_out, in_1[1], in_1[1]);
  nand nand_9 (nand_9_out, in_1[0], in_1[0]);
  nand nand_10 (nand_10_out, in_1[1], in_1[1]);
  nand nand_11 (nand_11_out, in_1[2], in_1[2]);
  nand nand_12 (nand_12_out, in_1[1], in_1[1]);
  nand nand_13 (nand_13_out, in_1[2], in_1[2]);
  nand nand_14 (nand_14_out, in_1[1], in_1[1]);
  nand nand_15 (nand_15_out, in_1[3], in_1[3]);
  nand nand_16 (nand_16_out, in_1[2], in_1[2]);
  nand nand_17 (nand_17_out, in_1[3], in_1[3]);
  nand nand_18 (nand_18_out, in_1[0], in_1[0]);
  nand nand_19 (nand_19_out, in_1[1], in_1[1]);
  not not_8 (not_8_out, in_1[3]);
  nand nand_20 (nand_20_out, in_1[3], in_1[2], in_1[1], in_1[0]);
  nand nand_21 (nand_21_out, in_1[3], in_1[2], in_1[1], in_1[0]);
  and and_1 (and_1_out, in_1[3], not_1_out);
  or or_1 (ALUsrc, and_1_out, and_2_out);
  and and_2 (and_2_out, in_1[3], in_1[2], in_1[0]);
  not not_9 (not_9_out, in_1[3]);
  or or_2 (ALUop, not_9_out, and_3_out);
  and and_3 (and_3_out, not_2_out, not_3_out);
  nand nand_22 (nand_22_out, in_1[3], nand_1_out, nand_2_out, nand_3_out);
  nand nand_23 (nand_23_out, in_1[3], in_1[2], in_1[1], in_1[0]);
  and and_4 (and_4_out, not_4_out, not_5_out, in_1[1], in_1[0]);
  and and_5 (and_5_out, in_1[3], not_6_out, not_7_out, in_1[0]);
  nand nand_24 (nand_24_out, nand_4_out, nand_5_out);
  nand nand_25 (nand_25_out, nand_6_out, nand_7_out);
  nand nand_26 (nand_26_out, nand_8_out, nand_9_out);
  nand nand_27 (nand_27_out, in_1[2], nand_10_out);
  nand nand_28 (nand_28_out, in_1[3], nand_11_out, nand_12_out);
  nand nand_29 (nand_29_out, in_1[3], nand_13_out, nand_14_out);
  nand nand_30 (nand_30_out, nand_15_out, nand_16_out);
  nand nand_31 (nand_31_out, nand_17_out, nand_18_out);
  nand nand_32 (nand_32_out, in_1[2], nand_19_out);
  and and_6 (Branch, not_8_out, in_1[2], in_1[1], in_1[0]);
  nand nand_33 (Jump, nand_20_out, nand_21_out);
  nand nand_34 (memRead, nand_22_out, nand_23_out);
  or or_3 (memWrite, and_4_out, and_5_out);
  nand nand_35 (RegWrite, nand_24_out, nand_25_out, nand_26_out, nand_27_out);
  nand nand_36 (memToReg, nand_28_out, nand_29_out);
  nand nand_37 (RegDst, nand_30_out, nand_31_out, nand_32_out);
endmodule

module Instruction_Block (
  input  [15:0] Instruction,
  output [2:0] Opcode,
  output [2:0] Rs,
  output [2:0] Rt,
  output [2:0] Rd,
  output [1:0] Shift_Amount,
  output [1:0] Function,
  output [6:0] Immediate
);


  assign Function = Instruction[1:0];
  assign Immediate = Instruction[6:0];
  assign Opcode = Instruction[15:13];
  assign Rd = Instruction[6:4];
  assign Rs = Instruction[12:10];
  assign Rt = Instruction[9:7];
  assign Shift_Amount = Instruction[3:2];
endmodule

module Control_Unit (
  input  [3:0] in_1,
  output ALUsrc,
  output ALUop,
  output memRead,
  output memWrite,
  output RegWrite,
  output memToReg,
  output RegDst,
  output Branch,
  output Jump
);

  wire and_1_out, and_2_out, and_3_out, and_4_out, and_5_out, and_6_out, and_7_out, and_8_out, and_9_out,
       and_10_out, and_11_out, and_12_out, and_13_out, and_14_out, and_15_out, and_16_out, and_17_out,
       and_18_out, and_19_out, and_20_out, and_21_out, and_22_out, and_23_out, and_24_out, nand_1_out,
       nand_2_out, nand_3_out, nand_4_out, nand_5_out, nand_6_out, nand_7_out, nand_8_out, nand_9_out,
       nand_10_out, nand_11_out, nand_12_out, nand_13_out, nand_14_out, nand_15_out, nand_16_out,
       nand_17_out, nand_18_out, nand_19_out, nand_20_out, nand_21_out, nand_22_out, nand_23_out,
       nand_24_out, nand_25_out, nand_26_out, nand_27_out, nand_28_out, nand_29_out, nand_30_out,
       nand_31_out, nand_32_out, not_1_out, not_3_out, not_4_out, not_5_out, not_6_out, not_7_out;

  not not_1 (not_1_out, in_1[1]);
  and and_1 (and_1_out, in_1[3], in_1[2]);
  not not_2 (ALUop, in_1[3]);
  nand nand_1 (nand_1_out, in_1[2], in_1[2]);
  nand nand_2 (nand_2_out, in_1[1], in_1[1]);
  nand nand_3 (nand_3_out, in_1[0], in_1[0]);
  not not_3 (not_3_out, in_1[3]);
  not not_4 (not_4_out, in_1[2]);
  not not_5 (not_5_out, in_1[2]);
  not not_6 (not_6_out, in_1[1]);
  nand nand_4 (nand_4_out, in_1[3], in_1[3]);
  nand nand_5 (nand_5_out, in_1[2], in_1[2]);
  nand nand_6 (nand_6_out, in_1[3], in_1[3]);
  nand nand_7 (nand_7_out, in_1[0], in_1[0]);
  nand nand_8 (nand_8_out, in_1[1], in_1[1]);
  nand nand_9 (nand_9_out, in_1[0], in_1[0]);
  nand nand_10 (nand_10_out, in_1[1], in_1[1]);
  nand nand_11 (nand_11_out, in_1[2], in_1[2]);
  nand nand_12 (nand_12_out, in_1[2], in_1[2]);
  nand nand_13 (nand_13_out, in_1[3], in_1[3]);
  nand nand_14 (nand_14_out, in_1[2], in_1[2]);
  nand nand_15 (nand_15_out, in_1[3], in_1[3]);
  nand nand_16 (nand_16_out, in_1[0], in_1[0]);
  not not_7 (not_7_out, in_1[3]);
  and and_2 (and_2_out, in_1[3], in_1[2]);
  and and_3 (and_3_out, in_1[1], in_1[0]);
  and and_4 (and_4_out, in_1[3], in_1[2]);
  and and_5 (and_5_out, in_1[1], in_1[0]);
  and and_6 (and_6_out, in_1[3], not_1_out);
  and and_7 (and_7_out, and_1_out, in_1[0]);
  and and_8 (and_8_out, in_1[3], nand_1_out);
  and and_9 (and_9_out, nand_2_out, nand_3_out);
  and and_10 (and_10_out, in_1[3], in_1[2]);
  and and_11 (and_11_out, in_1[1], in_1[0]);
  and and_12 (and_12_out, not_3_out, not_4_out);
  and and_13 (and_13_out, in_1[1], in_1[0]);
  and and_14 (and_14_out, in_1[3], not_5_out);
  and and_15 (and_15_out, not_6_out, in_1[0]);
  nand nand_17 (nand_17_out, nand_4_out, nand_5_out);
  nand nand_18 (nand_18_out, nand_6_out, nand_7_out);
  nand nand_19 (nand_19_out, nand_8_out, nand_9_out);
  nand nand_20 (nand_20_out, in_1[2], nand_10_out);
  and and_16 (and_16_out, in_1[3], nand_11_out);
  nand nand_21 (nand_21_out, in_1[1], in_1[1]);
  and and_17 (and_17_out, in_1[3], nand_12_out);
  nand nand_22 (nand_22_out, in_1[1], in_1[1]);
  nand nand_23 (nand_23_out, nand_13_out, nand_14_out);
  nand nand_24 (nand_24_out, nand_15_out, nand_16_out);
  nand nand_25 (nand_25_out, in_1[1], in_1[1]);
  and and_18 (and_18_out, not_7_out, in_1[2]);
  and and_19 (and_19_out, in_1[1], in_1[0]);
  nand nand_26 (nand_26_out, and_2_out, and_3_out);
  nand nand_27 (nand_27_out, and_4_out, and_5_out);
  or or_1 (ALUsrc, and_6_out, and_7_out);
  nand nand_28 (nand_28_out, and_8_out, and_9_out);
  nand nand_29 (nand_29_out, and_10_out, and_11_out);
  and and_20 (and_20_out, and_12_out, and_13_out);
  and and_21 (and_21_out, and_14_out, and_15_out);
  and and_22 (and_22_out, nand_17_out, nand_18_out);
  and and_23 (and_23_out, nand_19_out, nand_20_out);
  nand nand_30 (nand_30_out, and_16_out, nand_21_out);
  nand nand_31 (nand_31_out, and_17_out, nand_22_out);
  and and_24 (and_24_out, nand_23_out, nand_24_out);
  nand nand_32 (nand_32_out, in_1[2], nand_25_out);
  and and_25 (Branch, and_18_out, and_19_out);
  nand nand_33 (Jump, nand_26_out, nand_27_out);
  nand nand_34 (memRead, nand_28_out, nand_29_out);
  or or_2 (memWrite, and_20_out, and_21_out);
  nand nand_35 (RegWrite, and_22_out, and_23_out);
  nand nand_36 (memToReg, nand_30_out, nand_31_out);
  nand nand_37 (RegDst, and_24_out, nand_32_out);
endmodule
