// Logisim project alu control.circ as structural Verilog: 1 circuit, main circuit main
// ALUcontrol
module main (
  input  ALUop,
  input  I3,
  input  I2,
  input  I1,
  input  I0,
  output O2,
  output O1,
  output O0,
  output Enable
);

  wire and_1_out, and_2_out, and_3_out, nand_1_out, nand_2_out, nand_3_out, nand_5_out, nand_6_out,
       not_1_out, not_2_out, not_3_out;

  nand nand_1 (nand_1_out, I2, I2);
  nand nand_2 (nand_2_out, I3, I3);
  nand nand_3 (nand_3_out, I3, I3);
  not not_1 (not_1_out, I3);
  not not_2 (not_2_out, I1);
  not not_3 (not_3_out, I0);
  nand nand_4 (O2, nand_1_out, nand_2_out);
  nand nand_5 (nand_5_out, nand_3_out, I0);
  nand nand_6 (nand_6_out, I2, I0);
  and and_1 (and_1_out, ALUop, not_1_out);
  and and_2 (and_2_out, ALUop, not_2_out);
  and and_3 (and_3_out, ALUop, I2, not_3_out);
  nand nand_7 (O0, nand_5_out, nand_6_out);
  or or_1 (Enable, and_1_out, and_2_out, and_3_out);

  assign O1 = I1;
endmodule
